// Logisim project 1B_FullAdder.circ as structural Verilog: 1 circuit, main circuit main
module main (
  input  A,
  input  B,
  input  C_in,
  output C_out,
  output S
);

  wire and_1_out, and_2_out, and_3_out;

  and and_1 (and_1_out, A, C_in);
  and and_2 (and_2_out, A, B);
  and and_3 (and_3_out, C_in, B);
  xor xor_1 (S, A, B, C_in);
  or or_1 (C_out, and_1_out, and_2_out, and_3_out);
endmodule
