// Logisim project 4B_Calculator.circ as structural Verilog: 2 circuits, main circuit main
module main (
  input  B1,
  input  B2,
  input  B3,
  input  B4,
  input  Sub,
  input  A1,
  input  A2,
  input  A3,
  input  A4,
  output S1,
  output S2,
  output S3,
  output S4,
  output C_out
);

  wire fulladder_1_c_out, fulladder_2_c_out, fulladder_3_c_out, xor_1_out, xor_2_out, xor_3_out, xor_4_out;

  xor xor_1 (xor_1_out, Sub, B1);
  xor xor_2 (xor_2_out, Sub, B2);
  FullAdder fulladder_1 (.A(A1), .B(xor_1_out), .C_in(Sub), .C_out(fulladder_1_c_out), .S(S1));
  xor xor_3 (xor_3_out, Sub, B3);
  FullAdder fulladder_2 (.A(A2), .B(xor_2_out), .C_in(fulladder_1_c_out), .C_out(fulladder_2_c_out), .S(S2));
  xor xor_4 (xor_4_out, Sub, B4);
  FullAdder fulladder_3 (.A(A3), .B(xor_3_out), .C_in(fulladder_2_c_out), .C_out(fulladder_3_c_out), .S(S3));
  FullAdder fulladder_4 (.A(A4), .B(xor_4_out), .C_in(fulladder_3_c_out), .C_out(C_out), .S(S4));
endmodule

module FullAdder (
  input  A,
  input  B,
  input  C_in,
  output C_out,
  output S
);

  wire and_1_out, and_2_out, and_3_out;

  and and_1 (and_1_out, A, C_in);
  and and_2 (and_2_out, A, B);
  and and_3 (and_3_out, C_in, B);
  xor xor_1 (S, A, B, C_in);
  or or_1 (C_out, and_1_out, and_2_out, and_3_out);
endmodule
